// Logisim project eca_logisim_circuit.circ as structural Verilog: 10 circuits, main circuit main
module main (
  input  [7:0] Program,
  input  Reset,
  input  Set,
  input  Set_2,
  input  Set_3,
  input  Set_4,
  input  Set_5,
  input  Set_6,
  input  Set_7,
  input  Set_8
);

  wire clock_1_out, decoder_program_subcircuit_1_out_to_led, decoder_program_subcircuit_2_out_to_led,
       decoder_program_subcircuit_3_out_to_led, decoder_program_subcircuit_4_out_to_led,
       decoder_program_subcircuit_5_out_to_led, decoder_program_subcircuit_6_out_to_led,
       decoder_program_subcircuit_7_out_to_led, decoder_program_subcircuit_8_out_to_led;

  decoder___program_subcircuit decoder_program_subcircuit_1 (
    .In_from_self(decoder_program_subcircuit_1_out_to_led), .CLK(clock_1_out),
    .In_from_Left(decoder_program_subcircuit_8_out_to_led),
    .In_from_Right(decoder_program_subcircuit_2_out_to_led), .input_from_DIP(Program), .Set(Set),
    .Reset(Reset), .Out_to_LED(decoder_program_subcircuit_1_out_to_led));
  decoder___program_subcircuit decoder_program_subcircuit_2 (
    .In_from_self(decoder_program_subcircuit_2_out_to_led), .CLK(clock_1_out),
    .In_from_Left(decoder_program_subcircuit_1_out_to_led),
    .In_from_Right(decoder_program_subcircuit_3_out_to_led), .input_from_DIP(Program), .Set(Set_2),
    .Reset(Reset), .Out_to_LED(decoder_program_subcircuit_2_out_to_led));
  decoder___program_subcircuit decoder_program_subcircuit_3 (
    .In_from_self(decoder_program_subcircuit_3_out_to_led), .CLK(clock_1_out),
    .In_from_Left(decoder_program_subcircuit_2_out_to_led),
    .In_from_Right(decoder_program_subcircuit_4_out_to_led), .input_from_DIP(Program), .Set(Set_3),
    .Reset(Reset), .Out_to_LED(decoder_program_subcircuit_3_out_to_led));
  decoder___program_subcircuit decoder_program_subcircuit_4 (
    .In_from_self(decoder_program_subcircuit_4_out_to_led), .CLK(clock_1_out),
    .In_from_Left(decoder_program_subcircuit_3_out_to_led),
    .In_from_Right(decoder_program_subcircuit_5_out_to_led), .input_from_DIP(Program), .Set(Set_4),
    .Reset(Reset), .Out_to_LED(decoder_program_subcircuit_4_out_to_led));
  decoder___program_subcircuit decoder_program_subcircuit_5 (
    .In_from_self(decoder_program_subcircuit_5_out_to_led), .CLK(clock_1_out),
    .In_from_Left(decoder_program_subcircuit_4_out_to_led),
    .In_from_Right(decoder_program_subcircuit_6_out_to_led), .input_from_DIP(Program), .Set(Set_5),
    .Reset(Reset), .Out_to_LED(decoder_program_subcircuit_5_out_to_led));
  decoder___program_subcircuit decoder_program_subcircuit_6 (
    .In_from_self(decoder_program_subcircuit_6_out_to_led), .CLK(clock_1_out),
    .In_from_Left(decoder_program_subcircuit_5_out_to_led),
    .In_from_Right(decoder_program_subcircuit_7_out_to_led), .input_from_DIP(Program), .Set(Set_6),
    .Reset(Reset), .Out_to_LED(decoder_program_subcircuit_6_out_to_led));
  decoder___program_subcircuit decoder_program_subcircuit_7 (
    .In_from_self(decoder_program_subcircuit_7_out_to_led), .CLK(clock_1_out),
    .In_from_Left(decoder_program_subcircuit_6_out_to_led),
    .In_from_Right(decoder_program_subcircuit_8_out_to_led), .input_from_DIP(Program), .Set(Set_7),
    .Reset(Reset), .Out_to_LED(decoder_program_subcircuit_7_out_to_led));
  decoder___program_subcircuit decoder_program_subcircuit_8 (
    .In_from_self(decoder_program_subcircuit_8_out_to_led), .CLK(clock_1_out),
    .In_from_Left(decoder_program_subcircuit_7_out_to_led),
    .In_from_Right(decoder_program_subcircuit_1_out_to_led), .input_from_DIP(Program), .Set(Set_8),
    .Reset(Reset), .Out_to_LED(decoder_program_subcircuit_8_out_to_led));
  Clock clock_1 (.out(clock_1_out));
  LED led_1 (.in(decoder_program_subcircuit_8_out_to_led));
  LED led_2 (.in(decoder_program_subcircuit_7_out_to_led));
  LED led_3 (.in(decoder_program_subcircuit_5_out_to_led));
  LED led_4 (.in(decoder_program_subcircuit_4_out_to_led));
  LED led_5 (.in(decoder_program_subcircuit_3_out_to_led));
  LED led_6 (.in(decoder_program_subcircuit_6_out_to_led));
  LED led_7 (.in(decoder_program_subcircuit_1_out_to_led));
  LED led_8 (.in(decoder_program_subcircuit_2_out_to_led));
endmodule

// 4x2AND
module MM74HC08MX_4x2AND (
  input  [7:0] In,
  output [3:0] Out
);

  and and_1 (Out[0], In[0], In[1]);
  and and_2 (Out[1], In[2], In[3]);
  and and_3 (Out[2], In[4], In[5]);
  and and_4 (Out[3], In[6], In[7]);
endmodule

// 8-in OR
module CD4078BM_8_in_OR (
  input  [7:0] Input,
  output OR,
  output NOR
);

  or or_1 (OR, Input[0], Input[1], Input[2], Input[3], Input[4], Input[5], Input[6], Input[7]);
  not not_1 (NOR, OR);
endmodule

// 3x3 AND
module CD4073BE_3x3AND (
  input  [8:0] In,
  output [2:0] Out
);

  and and_1 (Out[0], In[0], In[1], In[2]);
  and and_2 (Out[1], In[3], In[4], In[5]);
  and and_3 (Out[2], In[6], In[7], In[8]);
endmodule

// NOT
module _74HC1GU04GV125_inverter (
  input  In,
  output Out
);

  not not_1 (Out, In);
endmodule

// DFF
module _74LVC1G74DP125_DFF (
  input  CLK,
  input  D,
  input  Set,
  input  Reset,
  output Q,
  output nQ
);

  D_Flip_Flop d_ff_1 (.clk(CLK), .D(D), .Q(Q), .Qn(nQ), .preset(Set), .reset(Reset));  // open: en
endmodule

module decoder___program_subcircuit (
  input  In_from_Left,
  input  In_from_self,
  input  In_from_Right,
  input  CLK,
  input  [7:0] input_from_DIP,
  input  Set,
  input  Reset,
  output Out_to_LED
);

  wire cd4078bm_8_in_or_1_or;
  wire [1:1] n74hc1gu04gv125_inverter_2_out;
  wire [2:0] n74hc1gu04gv125_inverter_1_out;
  wire [7:0] cd74hc237m96_2x4and_1_out0;

  _74HC1GU04GV125_inverter u_74hc1gu04gv125_inverter_1 (.In(In_from_Left), .Out(n74hc1gu04gv125_inverter_1_out[2]));
  _74HC1GU04GV125_inverter u_74hc1gu04gv125_inverter_2 (.In(In_from_self), .Out(n74hc1gu04gv125_inverter_2_out[1]));
  _74HC1GU04GV125_inverter u_74hc1gu04gv125_inverter_3 (.In(In_from_Right), .Out(n74hc1gu04gv125_inverter_1_out[0]));
  CD74HC237M96_2x4AND cd74hc237m96_2x4and_1 (
    .input0({input_from_DIP[0], n74hc1gu04gv125_inverter_1_out[2], n74hc1gu04gv125_inverter_2_out[1], n74hc1gu04gv125_inverter_1_out[0]}),
    .input1({input_from_DIP[1], n74hc1gu04gv125_inverter_1_out[2], n74hc1gu04gv125_inverter_2_out[1], In_from_Right}),
    .out0(cd74hc237m96_2x4and_1_out0[0]), .out1(cd74hc237m96_2x4and_1_out0[1]));
  CD74HC237M96_2x4AND cd74hc237m96_2x4and_2 (
    .input0({input_from_DIP[2], n74hc1gu04gv125_inverter_1_out[2], In_from_self, n74hc1gu04gv125_inverter_1_out[0]}),
    .input1({input_from_DIP[3], n74hc1gu04gv125_inverter_1_out[2], In_from_self, In_from_Right}),
    .out0(cd74hc237m96_2x4and_1_out0[2]), .out1(cd74hc237m96_2x4and_1_out0[3]));
  CD74HC237M96_2x4AND cd74hc237m96_2x4and_3 (
    .input0({input_from_DIP[4], In_from_Left, n74hc1gu04gv125_inverter_2_out[1], n74hc1gu04gv125_inverter_1_out[0]}),
    .input1({input_from_DIP[5], In_from_Left, n74hc1gu04gv125_inverter_2_out[1], In_from_Right}),
    .out0(cd74hc237m96_2x4and_1_out0[4]), .out1(cd74hc237m96_2x4and_1_out0[5]));
  CD74HC237M96_2x4AND cd74hc237m96_2x4and_4 (
    .input0({input_from_DIP[6], In_from_Left, In_from_self, n74hc1gu04gv125_inverter_1_out[0]}),
    .input1({input_from_DIP[7], In_from_Left, In_from_self, In_from_Right}),
    .out0(cd74hc237m96_2x4and_1_out0[6]), .out1(cd74hc237m96_2x4and_1_out0[7]));
  _74LVC1G74DP125_DFF u_74lvc1g74dp125_dff_1 (
    .CLK(CLK), .D(cd4078bm_8_in_or_1_or), .Set(Set), .Reset(Reset), .Q(Out_to_LED));  // open: nQ
  CD4078BM_8_in_OR cd4078bm_8_in_or_1 (.Input(cd74hc237m96_2x4and_1_out0), .OR(cd4078bm_8_in_or_1_or));  // open: NOR
  LED led_1 (.in(Out_to_LED));

  // Notes on the sheet:
  //   L
  //   M
  //   R
endmodule

module CD74HC237M96_2x4AND (
  input  [3:0] input0,
  input  [3:0] input1,
  output out0,
  output out1
);

  and and_1 (out0, input0[0], input0[1], input0[2], input0[3]);
  and and_2 (out1, input1[0], input1[1], input1[2], input1[3]);
endmodule

module old_decoder___program (
  input  In_from_Left,
  input  In_from_Right,
  input  CLK,
  input  [7:0] input_from_DIP,
  input  In_from_self,
  input  Set,
  input  Reset,
  output Out_to_LED
);

  wire cd4078bm_8_in_or_1_or;
  wire [2:0] cd4073be_3x3and_1_out, cd4073be_3x3and_2_out, cd4073be_3x3and_3_out;
  wire [3:0] mm74hc08mx_4x2and_1_out, mm74hc08mx_4x2and_2_out;
  wire [8:4] n74hc1gu04gv125_inverter_1_out;
  wire [8:6] undriven;

  _74HC1GU04GV125_inverter u_74hc1gu04gv125_inverter_1 (.In(In_from_Left), .Out(n74hc1gu04gv125_inverter_1_out[8]));
  _74HC1GU04GV125_inverter u_74hc1gu04gv125_inverter_2 (.In(In_from_self), .Out(n74hc1gu04gv125_inverter_1_out[4]));
  _74HC1GU04GV125_inverter u_74hc1gu04gv125_inverter_3 (.In(In_from_Right), .Out(n74hc1gu04gv125_inverter_1_out[6]));
  CD4073BE_3x3AND cd4073be_3x3and_1 (
    .In({n74hc1gu04gv125_inverter_1_out[8], In_from_self, n74hc1gu04gv125_inverter_1_out[6], n74hc1gu04gv125_inverter_1_out[8], n74hc1gu04gv125_inverter_1_out[4], In_from_Right, n74hc1gu04gv125_inverter_1_out[8], n74hc1gu04gv125_inverter_1_out[4], n74hc1gu04gv125_inverter_1_out[6]}),
    .Out(cd4073be_3x3and_1_out));
  CD4073BE_3x3AND cd4073be_3x3and_2 (
    .In({In_from_Left, n74hc1gu04gv125_inverter_1_out[4], In_from_Right, In_from_Left, n74hc1gu04gv125_inverter_1_out[4], n74hc1gu04gv125_inverter_1_out[6], n74hc1gu04gv125_inverter_1_out[8], In_from_self, In_from_Right}),
    .Out(cd4073be_3x3and_2_out));
  CD4073BE_3x3AND cd4073be_3x3and_3 (
    .In({undriven, In_from_Left, In_from_self, In_from_Right, In_from_Left, In_from_self, n74hc1gu04gv125_inverter_1_out[6]}),
    .Out(cd4073be_3x3and_3_out));
  MM74HC08MX_4x2AND mm74hc08mx_4x2and_1 (
    .In({input_from_DIP[3], cd4073be_3x3and_2_out[0], input_from_DIP[2], cd4073be_3x3and_1_out[2], input_from_DIP[1], cd4073be_3x3and_1_out[1], input_from_DIP[0], cd4073be_3x3and_1_out[0]}),
    .Out(mm74hc08mx_4x2and_1_out));
  MM74HC08MX_4x2AND mm74hc08mx_4x2and_2 (
    .In({input_from_DIP[7], cd4073be_3x3and_3_out[1], input_from_DIP[6], cd4073be_3x3and_3_out[0], input_from_DIP[5], cd4073be_3x3and_2_out[2], input_from_DIP[4], cd4073be_3x3and_2_out[1]}),
    .Out(mm74hc08mx_4x2and_2_out));
  _74LVC1G74DP125_DFF u_74lvc1g74dp125_dff_1 (
    .CLK(CLK), .D(cd4078bm_8_in_or_1_or), .Set(Set), .Reset(Reset), .Q(Out_to_LED));  // open: nQ
  CD4078BM_8_in_OR cd4078bm_8_in_or_1 (
    .Input({mm74hc08mx_4x2and_2_out, mm74hc08mx_4x2and_1_out}), .OR(cd4078bm_8_in_or_1_or));  // open: NOR

  // Notes on the sheet:
  //   L
  //   M
  //   R
endmodule

module equivalance (
);

  wire and_1_out, and_2_out, and_3_out, undriven, undriven_2, undriven_3, undriven_4, undriven_5, undriven_6,
       undriven_7, undriven_8;

  and and_1 (and_1_out, undriven, undriven_2, undriven_3);
  and and_2 (and_2_out, and_1_out, undriven_4);
  and and_3 (and_3_out, undriven_5, undriven_6, undriven_7, undriven_8);
endmodule
